# Fritzing sketch schema (saved by Fritzing 0.9.4)
breadboards: 1

parts:
  Mod1 = Raspberry Pi 4B
  J1 = Basic Servo
  Part1 = RFID-RC522-v2
  Mod2 = KY-012 Active Buzzer Module [package="Breakout board"]
  TFT1 = 1.44" SPI TFT Graphics Display 128x128 [package=THT]

nets:
  3V3: Mod1.3V3, Part1.3.3V
  5V: Mod1.5V, J1.vcc, Mod2.S, TFT1.5V
  GND: Mod1.GND, J1.gnd, Part1.GND, Mod2.-, TFT1.GND
  N1: Mod1.GPIO18, Part1.SDA
  N2: Mod1.GPIO10, TFT1.MOSI
  N3: Mod1.GPIO9, TFT1.MISO
  N4: Mod1.GPIO25, TFT1.CS
  N5: Mod1.GPIO11, TFT1.SCK
  N6: Mod1.GPIO7, TFT1.IRQ
  N7: Mod1.GPIO5, J1.pulse
  N8: Mod1.GPIO12, Mod2.NC
  N9: Mod1.GPIO19, Part1.MISO
  N10: Mod1.GPIO26, Part1.RST
  N11: Mod1.GPIO20, Part1.MOSI
  N12: Mod1.GPIO21, Part1.SCK

custom parts:
  RFID-RC522-v2: A simple China made RFID-RC522 Reader; do check the pin labels, as this is a MFRC522 based clone.
  KY-012 Active Buzzer Module: Active Piezoelectric Buzzer Module KY-012, it produces single-tone sound when signal is high. (Special thanks to vanepp for fixing the PCB holes and other errors)
  1.44" SPI TFT Graphics Display 128x128: This is for https://www.amazon.com/gp/product/B07B4BDWCL/ref=ask_ql_qh_dp_hza display. Note that this display is sold with a misprinted silkscreen indicating I2C connections on P2 connector, it is actualy SPI. The P1 connections are non functional on this board from the linked URL seller on Amazon.
